# Fritzing sketch pinning (saved by Fritzing 0.9.5d)

parts:
  M1 = STM32F103C8T6 blue mini board
  R2 = Resistor [tolerance=±5% power=0.25 resistance=4700 package=THT]
  Bauteil1 = InvenSense MPU6050
  R3 = Resistor [tolerance=±5% power=0.25 resistance=4700 package=THT]
  R4 = Resistor [tolerance=±5% power=0.25 resistance=1800 package=THT]

nets:
  N1: M1.A12, R4.Pin_0
  N2: M1.B6, Bauteil1.SCL, R3.Pin_0
  N3: M1.B7, R2.Pin_0, Bauteil1.SDA
  N4: M1.G, Bauteil1.GND
  3.3V: M1.3.3V, R2.Pin_1, Bauteil1.VCC, R3.Pin_1, R4.Pin_1

notes:
  Stepper1 Dir   B12
  Stepper1 Step B13
  Stepper2 Step B15
  Stepper2 Dir   B14
  Stepper3 Step  A9
  Stepper3 Dir    A8
  Stepper4 Step  B3
  Stepper4 Dir   A15
  SCL B6
  SDA B7
  4K7
  Analog 1
  Analog 2
  Analog 3
  Analog 4
  Analog 5
  Analog 6
  PWM 1
  PWM 2
  PWM 3
  PWM 4
  PWM 5
  PWM 6
  Optional 1.8k Pullup to A12
  For better USB detection
  Dir pin low when
  counting in positive direction
